// Logisim project bonkpu.circ as structural Verilog: 2 circuits, main circuit main
module main (
);

  wire and_1_out, and_2_out, and_3_out, button_1_out, CL_carry, CLK, clock_1_out, comparator_1_eq,
       dipswitch_1_p1, nor_2_out, not_1_out, not_2_out, or_1_out, or_2_out, xor_2_out;
  wire [2:0] FLAGS, nor_1_out;
  wire [3:0] MICROSTEP_q;
  wire [7:0] A_REG_q, adder_1_out, B_REG_q, CH_q, CL_q, controlled_buffer_1_out, MEM_dout, microcode_a_data,
       microcode_b_data, microcode_c_data, multiplexer_2_out, OP_REG_q, PROGMEM_data, xor_1_out;
  wire [14:0] MARL_q;
  wire [15:15] MARH_q;

  ROM #(.addrWidth(15)) PROGMEM (.addr(MARL_q), .data(PROGMEM_data));
  Counter #(.max('hf), .width(4)) MICROSTEP (
    .load(microcode_c_data[0]), .clk(not_1_out), .D(4'b0000), .Q(MICROSTEP_q));  // open: clr, up, count, carry
  not not_1 (not_1_out, CLK);
  and and_1 (and_1_out, microcode_b_data[2], CL_carry);
  or or_1 (or_1_out, microcode_c_data[6], microcode_b_data[2]);
  Register MARH (
    .D(controlled_buffer_1_out), .en(microcode_a_data[6]), .clk(CLK), .Q({MARH_q[15], MARL_q[14:8]}));  // open: clr
  or or_2 (or_2_out, microcode_c_data[7], and_1_out);
  Register OP_REG (.D(controlled_buffer_1_out), .en(microcode_a_data[2]), .clk(CLK), .Q(OP_REG_q));  // open: clr
  Register MARL (.D(controlled_buffer_1_out), .en(microcode_a_data[5]), .clk(CLK), .Q(MARL_q[7:0]));  // open: clr
  and and_2 (and_2_out, MARH_q[15], microcode_a_data[4]);
  RAM #(.addrWidth(15), .enables("line")) MEM (
    .addr(MARL_q), .we(and_2_out), .clk(CLK), .din(controlled_buffer_1_out), .dout(MEM_dout));
  Counter CH (
    .load(microcode_c_data[7]), .count(or_2_out), .clk(CLK), .D(controlled_buffer_1_out), .Q(CH_q));  // open: clr, up, carry
  Counter CL (
    .load(microcode_c_data[6]), .count(or_1_out), .clk(CLK), .D(controlled_buffer_1_out), .carry(CL_carry),
    .Q(CL_q));  // open: clr, up
  ROM #(.addrWidth(15)) microcode_a (.addr({FLAGS, OP_REG_q, MICROSTEP_q}), .data(microcode_a_data));
  assign controlled_buffer_1_out = microcode_b_data[1] ? CH_q : 8'bz;  // Controlled_Buffer controlled_buffer_1
  assign controlled_buffer_1_out = microcode_b_data[0] ? CL_q : 8'bz;  // Controlled_Buffer controlled_buffer_2
  Multiplexer #(.disabled("Z"), .enable("true"), .width(8)) multiplexer_1 (
    .in0(PROGMEM_data), .in1(MEM_dout), .out(controlled_buffer_1_out), .sel(MARH_q[15]),
    .en(microcode_a_data[3]));
  LedBar ledbar_1 (
    .led0(controlled_buffer_1_out[7]), .led1(controlled_buffer_1_out[6]), .led2(controlled_buffer_1_out[5]),
    .led3(controlled_buffer_1_out[4]), .led4(controlled_buffer_1_out[3]), .led5(controlled_buffer_1_out[2]),
    .led6(controlled_buffer_1_out[1]), .led7(controlled_buffer_1_out[0]));
  Pull_Resistor pull_resistor_1 (.node(controlled_buffer_1_out));
  ROM #(.addrWidth(15)) microcode_b (.addr({FLAGS, OP_REG_q, MICROSTEP_q}), .data(microcode_b_data));
  assign controlled_buffer_1_out = microcode_b_data[5] ? adder_1_out : 8'bz;  // Controlled_Buffer EO_GATE
  Register A_REG (.D(controlled_buffer_1_out), .en(microcode_a_data[1]), .clk(CLK), .Q(A_REG_q));  // open: clr
  assign controlled_buffer_1_out = microcode_a_data[0] ? A_REG_q : 8'bz;  // Controlled_Buffer controlled_buffer_3
  Register B_REG (.D(controlled_buffer_1_out), .en(microcode_b_data[7]), .clk(CLK), .Q(B_REG_q));  // open: clr
  assign controlled_buffer_1_out = microcode_b_data[6] ? B_REG_q : 8'bz;  // Controlled_Buffer B_GATE
  Multiplexer #(.width(8)) multiplexer_2 (
    .in0({8{1'b0}}), .in1({8{1'b1}}), .out(multiplexer_2_out), .sel(microcode_b_data[4]));
  ROM #(.addrWidth(15)) microcode_c (.addr({FLAGS, OP_REG_q, MICROSTEP_q}), .data(microcode_c_data));
  LedBar #(.matrixcols(24)) ledbar_2 (
    .led0(microcode_a_data[7]), .led1(microcode_a_data[6]), .led2(microcode_a_data[5]),
    .led3(microcode_a_data[4]), .led4(microcode_a_data[3]), .led5(microcode_a_data[2]),
    .led6(microcode_a_data[1]), .led7(microcode_a_data[0]), .led8(microcode_b_data[7]),
    .led9(microcode_b_data[6]), .led10(microcode_b_data[5]), .led11(microcode_b_data[4]),
    .led12(microcode_b_data[3]), .led13(microcode_b_data[2]), .led14(microcode_b_data[1]),
    .led15(microcode_b_data[0]), .led16(microcode_c_data[7]), .led17(microcode_c_data[6]),
    .led18(microcode_c_data[5]), .led19(microcode_c_data[4]), .led20(microcode_c_data[3]),
    .led21(microcode_c_data[2]), .led22(microcode_c_data[1]), .led23(microcode_c_data[0]));
  assign xor_1_out = multiplexer_2_out ^ B_REG_q;  // XOR_Gate xor_1, 8 bits wide
  // Probe on B_REG_q
  // Probe on B_REG_q
  // Probe on A_REG_q
  // Probe on A_REG_q
  Adder adder_1 (.a(A_REG_q), .b(xor_1_out), .out(adder_1_out), .cin(microcode_b_data[4]), .cout(nor_1_out[2]));
  stack_pointer stack_pointer_1 (
    .HO(microcode_c_data[3]), .LO(microcode_c_data[2]), .CLK(CLK), .MODE(microcode_c_data[5:4]),
    .out_bus(controlled_buffer_1_out));
  // Probe on adder_1_out
  // Probe on adder_1_out
  nor nor_1 (nor_1_out[0], adder_1_out[0], adder_1_out[1], adder_1_out[2], adder_1_out[3], adder_1_out[4], adder_1_out[5], adder_1_out[6], adder_1_out[7]);
  Clock clock_1 (.out(clock_1_out));
  Comparator #(.mode("unsigned"), .width(4)) comparator_1 (
    .a(MICROSTEP_q), .b(4'b0000), .eq(comparator_1_eq));  // open: gt, lt
  Register #(.width(3)) FLAG_REG (
    .D({nor_1_out[2], adder_1_out[7], nor_1_out[0]}), .en(microcode_b_data[3]), .clk(CLK), .Q(FLAGS));  // open: clr
  nor nor_2 (nor_2_out, microcode_a_data[7], and_3_out);
  and and_3 (and_3_out, comparator_1_eq, xor_2_out);
  LedBar #(.matrixcols(3)) ledbar_3 (.led0(FLAGS[2]), .led1(FLAGS[1]), .led2(FLAGS[0]));
  and and_4 (CLK, clock_1_out, nor_2_out);
  xor xor_2 (xor_2_out, button_1_out, not_2_out);
  not not_2 (not_2_out, dipswitch_1_p1);
  Button #(.press("passive")) button_1 (.out(button_1_out));
  // DipSwitch #(.number(2)) dipswitch_1: pin names not known; wires that end beside it: dipswitch_1_p1

  // Notes on the sheet:
  //   contents of PROGMEM (hex, n*v repeats v):
  //   f 1 1 14 15 0 14 12 0 14 f 0 8 18 0 4 4 15 4 3 15 4 2 15 16
  //   contents of microcode_a (hex, n*v repeats v):
  //   20 40 c 13*0 20 40 c 20 40 a 10*0 20 40 c 20 40 8 20 40 48 20 a 5*0 20 40 c 20 40 8 20 40 48 20 11
  //   5*0 20 40 c 20 40 8 2 9*0 20 40 c 20 40 8 20 40 48 20 8 2 4*0 20 40 c 20 40 8 2 9*0 20 40 c 20 40 8
  //   20 40 48 20 8 2 4*0 20 40 c 20 40 8 20 40 8 7*0 20 40 c 13*0 20 40 c 20 40 8 20 40 8 7*0 20 40 c
  //   13*0 20 40 c 20 40 8 20 40 8 7*0 20 40 c 13*0 20 40 c 20 40 8 20 40 8 7*0 20 40 c 13*0 20 40 c 13*0
  //   20 40 c 13*0 20 40 c 20 40 11 10*0 20 40 c 0 20 40 a 9*0 20 40 c 20 40 10 20 40 10 20 40 8 20 40 8 0
  //   20 40 c 0 20 40 8 20 40 8 6*0 20 40 c 80 12*0 20 40 c 13*0 20 40 c 13*0 20 40 c 13*0 20 40 c 13*0 20
  //   40 c 13*0 20 40 c 13*0 20 40 c 13*0 20 40 c 13*0 20 40 c 13*0 20 40 c 13*0 20 40 c 13*0 20 40 c 13*0
  //   20 40 c 13*0 20 40 c 13*0 20 40 c 13*0 20 40 c 13*0 20 40 c 13*0 20 40 c 13*0 20 40 c 13*0 20 40 c
  //   13*0 20 40 c 13*0 20 40 c 13*0 20 40 c 13*0 20 40 c 13*0 20 40 c 13*0 20 40 c 13*0 20 40 c 13*0 20
  //   40 c 13*0 20 40 c 13*0 20 40 c 13*0 20 40 c 13*0 20 40 c 13*0 20 40 c 13*0 20 40 c 13*0 20 40 c 13*0
  //   20 40 c 13*0 20 40 c 13*0 20 40 c 13*0 20 40 c 13*0 20 40 c 13*0 20 40 c 13*0 20 40 c 13*0 20 40 c
  //   13*0 20 40 c 13*0 20 40 c 13*0 20 40 c 13*0 20 40 c 13*0 20 40 c 13*0 20 40 c 13*0 20 40 c 13*0 20
  //   40 c 13*0 20 40 c 13*0 20 40 c 13*0 20 40 c 13*0 20 40 c 13*0 20 40 c 13*0 20 40 c 13*0 20 40 c 13*0
  //   20 40 c 13*0 20 40 c 13*0 20 40 c 13*0 20 40 c 13*0 20 40 c 13*0 20 40 c 13*0 20 40 c 13*0 20 40 c
  //   13*0 20 40 c 13*0 20 40 c 13*0 20 40 c 13*0 20 40 c 13*0 20 40 c 13*0 20 40 c 13*0 20 40 c 13*0 20
  //   40 c 13*0 20 40 c 13*0 20 40 c 13*0 20 40 c 13*0 20 40 c 13*0 20 40 c 13*0 20 40 c 13*0 20 40 c 13*0
  //   20 40 c 13*0 20 40 c 13*0 20 40 c 13*0 20 40 c 13*0 20 40 c 13*0 20 40 c 13*0 20 40 c 13*0 20 40 c
  //   13*0 20 40 c 13*0 20 40 c 13*0 20 40 c 13*0 20 40 c 13*0 20 40 c 13*0 20 40 c 13*0 20 40 c 13*0 20
  //   40 c 13*0 20 40 c 13*0 20 40 c 13*0 20 40 c 13*0 20 40 c 13*0 20 40 c 13*0 20 40 c 13*0 20 40 c 13*0
  //   20 40 c 13*0 20 40 c 13*0 20 40 c 13*0 20 40 c 13*0 20 40 c 13*0 20 40 c 13*0 20 40 c 13*0 20 40 c
  //   13*0 20 40 c 13*0 20 40 c 13*0 20 40 c 13*0 20 40 c 13*0 20 40 c 13*0 20 40 c 13*0 20 40 c 13*0 20
  //   40 c 13*0 20 40 c 13*0 20 40 c 13*0 20 40 c 13*0 20 40 c 13*0 20 40 c 13*0 20 40 c 13*0 20 40 c 13*0
  //   20 40 c 13*0 20 40 c 13*0 20 40 c 13*0 20 40 c 13*0 20 40 c 13*0 20 40 c 13*0 20 40 c 13*0 20 40 c
  //   13*0 20 40 c 13*0 20 40 c 13*0 20 40 c 13*0 20 40 c 13*0 20 40 c 13*0 20 40 c 13*0 20 40 c 13*0 20
  //   40 c 13*0 20 40 c 13*0 20 40 c 13*0 20 40 c 13*0 20 40 c 13*0 20 40 c 13*0 20 40 c 13*0 20 40 c 13*0
  //   20 40 c 13*0 20 40 c 13*0 20 40 c 13*0 20 40 c 13*0 20 40 c 13*0 20 40 c 13*0 20 40 c 13*0 20 40 c
  //   13*0 20 40 c 13*0 20 40 c 13*0 20 40 c 13*0 20 40 c 13*0 20 40 c 13*0 20 40 c 13*0 20 40 c 13*0 20
  //   40 c 13*0 20 40 c 13*0 20 40 c 13*0 20 40 c 13*0 20 40 c 13*0 20 40 c 13*0 20 40 c 13*0 20 40 c 13*0
  //   20 40 c 13*0 20 40 c 13*0 20 40 c 13*0 20 40 c 13*0 20 40 c 13*0 20 40 c 13*0 20 40 c 13*0 20 40 c
  //   13*0 20 40 c 13*0 20 40 c 13*0 20 40 c 13*0 20 40 c 13*0 20 40 c 13*0 20 40 c 13*0 20 40 c 13*0 20
  //   40 c 13*0 20 40 c 13*0 20 40 c 13*0 20 40 c 13*0 20 40 c 13*0 20 40 c 13*0 20 40 c 13*0 20 40 c 13*0
  //   20 40 c 13*0 20 40 c 13*0 20 40 c 13*0 20 40 c 13*0 20 40 c 13*0 20 40 c 13*0 20 40 c 13*0 20 40 c
  //   13*0 20 40 c 13*0 20 40 c 13*0 20 40 c 13*0 20 40 c 13*0 20 40 c 13*0 20 40 c 13*0 20 40 c 13*0 20
  //   40 c 13*0 20 40 c 13*0 20 40 c 13*0 20 40 c 13*0 20 40 c 13*0 20 40 c 13*0 20 40 c 13*0 20 40 c 13*0
  //   20 40 c 13*0 20 40 c 13*0 20 40 c 13*0 20 40 c 13*0 20 40 c 13*0 20 40 c 13*0 20 40 c 13*0 20 40 c
  //   13*0 20 40 c 13*0 20 40 c 13*0 20 40 c 13*0 20 40 c 13*0 20 40 c 13*0 20 40 c 13*0 20 40 c 13*0 20
  //   40 c 20 40 a 10*0 20 40 c 20 40 8 20 40 48 20 a 5*0 20 40 c 20 40 8 20 40 48 20 11 5*0 20 40 c 20 40
  //   8 2 9*0 20 40 c 20 40 8 20 40 48 20 8 2 4*0 20 40 c 20 40 8 2 9*0 20 40 c 20 40 8 20 40 48 20 8 2
  //   4*0 20 40 c 20 40 8 20 40 8 7*0 20 40 c 20 40 8 20 40 8 7*0 20 40 c 13*0 20 40 c 13*0 20 40 c 20 40
  //   8 20 40 8 7*0 20 40 c 13*0 20 40 c 20 40 8 20 40 8 7*0 20 40 c 13*0 20 40 c 13*0 20 40 c 13*0 20 40
  //   c 20 40 11 10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
  //   contents of microcode_b (hex, n*v repeats v):
  //   1 2 4 13*0 1 2 4 1 2 4 10*0 1 2 4 1 2 84 1 2 4 40 6*0 1 2 4 1 2 84 1 2 4 40 6*0 1 2 4 1 2 84 28 9*0
  //   1 2 4 1 2 84 1 2 4 40 80 28 4*0 1 2 4 1 2 84 38 9*0 1 2 4 1 2 84 1 2 4 40 80 38 4*0 1 2 4 1 2 84 1 2
  //   4 40 6*0 1 2 4 4 4 11*0 1 2 4 1 2 84 1 2 4 40 6*0 1 2 4 4 4 11*0 1 2 4 1 2 84 1 2 4 40 6*0 1 2 4 4 4
  //   11*0 1 2 4 1 2 84 1 2 4 40 6*0 1 2 4 13*0 1 2 4 13*0 1 2 4 13*0 1 2 4 13*0 1 2 4 13*0 1 2 4 0 0 2 0
  //   0 1 1 2 84 1 2 4 40 1 2 4 7*0 4 4 4*0 1 2 4 13*0 1 2 4 13*0 1 2 4 13*0 1 2 4 13*0 1 2 4 13*0 1 2 4
  //   13*0 1 2 4 13*0 1 2 4 13*0 1 2 4 13*0 1 2 4 13*0 1 2 4 13*0 1 2 4 13*0 1 2 4 13*0 1 2 4 13*0 1 2 4
  //   13*0 1 2 4 13*0 1 2 4 13*0 1 2 4 13*0 1 2 4 13*0 1 2 4 13*0 1 2 4 13*0 1 2 4 13*0 1 2 4 13*0 1 2 4
  //   13*0 1 2 4 13*0 1 2 4 13*0 1 2 4 13*0 1 2 4 13*0 1 2 4 13*0 1 2 4 13*0 1 2 4 13*0 1 2 4 13*0 1 2 4
  //   13*0 1 2 4 13*0 1 2 4 13*0 1 2 4 13*0 1 2 4 13*0 1 2 4 13*0 1 2 4 13*0 1 2 4 13*0 1 2 4 13*0 1 2 4
  //   13*0 1 2 4 13*0 1 2 4 13*0 1 2 4 13*0 1 2 4 13*0 1 2 4 13*0 1 2 4 13*0 1 2 4 13*0 1 2 4 13*0 1 2 4
  //   13*0 1 2 4 13*0 1 2 4 13*0 1 2 4 13*0 1 2 4 13*0 1 2 4 13*0 1 2 4 13*0 1 2 4 13*0 1 2 4 13*0 1 2 4
  //   13*0 1 2 4 13*0 1 2 4 13*0 1 2 4 13*0 1 2 4 13*0 1 2 4 13*0 1 2 4 13*0 1 2 4 13*0 1 2 4 13*0 1 2 4
  //   13*0 1 2 4 13*0 1 2 4 13*0 1 2 4 13*0 1 2 4 13*0 1 2 4 13*0 1 2 4 13*0 1 2 4 13*0 1 2 4 13*0 1 2 4
  //   13*0 1 2 4 13*0 1 2 4 13*0 1 2 4 13*0 1 2 4 13*0 1 2 4 13*0 1 2 4 13*0 1 2 4 13*0 1 2 4 13*0 1 2 4
  //   13*0 1 2 4 13*0 1 2 4 13*0 1 2 4 13*0 1 2 4 13*0 1 2 4 13*0 1 2 4 13*0 1 2 4 13*0 1 2 4 13*0 1 2 4
  //   13*0 1 2 4 13*0 1 2 4 13*0 1 2 4 13*0 1 2 4 13*0 1 2 4 13*0 1 2 4 13*0 1 2 4 13*0 1 2 4 13*0 1 2 4
  //   13*0 1 2 4 13*0 1 2 4 13*0 1 2 4 13*0 1 2 4 13*0 1 2 4 13*0 1 2 4 13*0 1 2 4 13*0 1 2 4 13*0 1 2 4
  //   13*0 1 2 4 13*0 1 2 4 13*0 1 2 4 13*0 1 2 4 13*0 1 2 4 13*0 1 2 4 13*0 1 2 4 13*0 1 2 4 13*0 1 2 4
  //   13*0 1 2 4 13*0 1 2 4 13*0 1 2 4 13*0 1 2 4 13*0 1 2 4 13*0 1 2 4 13*0 1 2 4 13*0 1 2 4 13*0 1 2 4
  //   13*0 1 2 4 13*0 1 2 4 13*0 1 2 4 13*0 1 2 4 13*0 1 2 4 13*0 1 2 4 13*0 1 2 4 13*0 1 2 4 13*0 1 2 4
  //   13*0 1 2 4 13*0 1 2 4 13*0 1 2 4 13*0 1 2 4 13*0 1 2 4 13*0 1 2 4 13*0 1 2 4 13*0 1 2 4 13*0 1 2 4
  //   13*0 1 2 4 13*0 1 2 4 13*0 1 2 4 13*0 1 2 4 13*0 1 2 4 13*0 1 2 4 13*0 1 2 4 13*0 1 2 4 13*0 1 2 4
  //   13*0 1 2 4 13*0 1 2 4 13*0 1 2 4 13*0 1 2 4 13*0 1 2 4 13*0 1 2 4 13*0 1 2 4 13*0 1 2 4 13*0 1 2 4
  //   13*0 1 2 4 13*0 1 2 4 13*0 1 2 4 13*0 1 2 4 13*0 1 2 4 13*0 1 2 4 13*0 1 2 4 13*0 1 2 4 13*0 1 2 4
  //   13*0 1 2 4 13*0 1 2 4 13*0 1 2 4 13*0 1 2 4 13*0 1 2 4 13*0 1 2 4 13*0 1 2 4 13*0 1 2 4 13*0 1 2 4
  //   13*0 1 2 4 13*0 1 2 4 13*0 1 2 4 13*0 1 2 4 13*0 1 2 4 13*0 1 2 4 13*0 1 2 4 13*0 1 2 4 13*0 1 2 4
  //   13*0 1 2 4 13*0 1 2 4 13*0 1 2 4 13*0 1 2 4 13*0 1 2 4 13*0 1 2 4 13*0 1 2 4 13*0 1 2 4 13*0 1 2 4
  //   13*0 1 2 4 13*0 1 2 4 13*0 1 2 4 13*0 1 2 4 13*0 1 2 4 13*0 1 2 4 13*0 1 2 4 13*0 1 2 4 13*0 1 2 4
  //   13*0 1 2 4 13*0 1 2 4 13*0 1 2 4 13*0 1 2 4 13*0 1 2 4 13*0 1 2 4 13*0 1 2 4 13*0 1 2 4 13*0 1 2 4
  //   13*0 1 2 4 13*0 1 2 4 13*0 1 2 4 13*0 1 2 4 13*0 1 2 4 13*0 1 2 4 13*0 1 2 4 13*0 1 2 4 13*0 1 2 4
  //   13*0 1 2 4 13*0 1 2 4 13*0 1 2 4 13*0 1 2 4 13*0 1 2 4 1 2 4 10*0 1 2 4 1 2 84 1 2 4 40 6*0 1 2 4 1
  //   2 84 1 2 4 40 6*0 1 2 4 1 2 84 28 9*0 1 2 4 1 2 84 1 2 4 40 80 28 4*0 1 2 4 1 2 84 38 9*0 1 2 4 1 2
  //   84 1 2 4 40 80 38 4*0 1 2 4 1 2 84 1 2 4 40 6*0 1 2 4 1 2 84 1 2 4 40 6*0 1 2 4 4 4 11*0 1 2 4 4 4
  //   11*0 1 2 4 1 2 84 1 2 4 40 6*0 1 2 4 4 4 11*0 1 2 4 1 2 84 1 2 4 40 6*0 1 2 4 13*0 1 2 4 13*0 1 2 4
  //   13*0 1 2 4 13*0 1 2 4 13*0 1 2 4 0 0 2 0 0 1 1 2 84 1 2 4 40 1 2 4 7*0 4 4 4*0 1 2 4 13*0 1 2 4 13*0
  //   1 2 4 13*0 1 2 4 13*0 1 2 4 13*0 1 2 4 13*0 1 2 4 13*0 1 2 4 13*0 1 2 4 13*0 1 2 4 13*0 1 2 4 13*0 1
  //   2 4 13*0 1 2 4 13*0 1 2 4 13*0 1 2 4 13*0 1 2 4 13*0 1 2 4 13*0 1 2 4 13*0 1 2 4 13*0 1 2 4 13*0 1 2
  //   4 13*0 1 2 4 13*0 1 2 4 13*0 1 2 4 13*0 1 2 4 13*0 1 2 4 13*0 1 2 4 13*0 1 2 4 13*0 1 2 4 13*0 1 2 4
  //   13*0 1 2 4 13*0 1 2 4 13*0 1 2 4 13*0 1 2 4 13*0 1 2 4 13*0 1 2 4 13*0 1 2 4 13*0 1 2 4 13*0 1 2 4
  //   13*0 1 2 4 13*0 1 2 4 13*0 1 2 4 13*0 1 2 4 13*0 1 2 4 13*0 1 2 4 13*0 1 2 4 13*0 1 2 4 13*0 1 2 4
  //   13*0 1 2 4 13*0 1 2 4 1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
  //   contents of microcode_c (hex, n*v repeats v):
  //   0 0 1 18*0 1 20*0 1 15*0 1 11*0 1 20*0 1 10*0 1 20*0 1 12*0 80 41 10*0 1 19*0 80 41 10*0 1 19*0 80
  //   41 10*0 1 19*0 80 41 9*0 11 15*0 31 15*0 21 15*0 4 8 31 13*0 20 4 8 1 12*0 4 8 30 4 8 30 5*0 80 41 0
  //   0 0 20 4 8 60 4 8 80 0 1 7*0 1 14*0 1 15*0 1 15*0 1 15*0 1 15*0 1 15*0 1 15*0 1 15*0 1 15*0 1 15*0 1
  //   15*0 1 15*0 1 15*0 1 15*0 1 15*0 1 15*0 1 15*0 1 15*0 1 15*0 1 15*0 1 15*0 1 15*0 1 15*0 1 15*0 1
  //   15*0 1 15*0 1 15*0 1 15*0 1 15*0 1 15*0 1 15*0 1 15*0 1 15*0 1 15*0 1 15*0 1 15*0 1 15*0 1 15*0 1
  //   15*0 1 15*0 1 15*0 1 15*0 1 15*0 1 15*0 1 15*0 1 15*0 1 15*0 1 15*0 1 15*0 1 15*0 1 15*0 1 15*0 1
  //   15*0 1 15*0 1 15*0 1 15*0 1 15*0 1 15*0 1 15*0 1 15*0 1 15*0 1 15*0 1 15*0 1 15*0 1 15*0 1 15*0 1
  //   15*0 1 15*0 1 15*0 1 15*0 1 15*0 1 15*0 1 15*0 1 15*0 1 15*0 1 15*0 1 15*0 1 15*0 1 15*0 1 15*0 1
  //   15*0 1 15*0 1 15*0 1 15*0 1 15*0 1 15*0 1 15*0 1 15*0 1 15*0 1 15*0 1 15*0 1 15*0 1 15*0 1 15*0 1
  //   15*0 1 15*0 1 15*0 1 15*0 1 15*0 1 15*0 1 15*0 1 15*0 1 15*0 1 15*0 1 15*0 1 15*0 1 15*0 1 15*0 1
  //   15*0 1 15*0 1 15*0 1 15*0 1 15*0 1 15*0 1 15*0 1 15*0 1 15*0 1 15*0 1 15*0 1 15*0 1 15*0 1 15*0 1
  //   15*0 1 15*0 1 15*0 1 15*0 1 15*0 1 15*0 1 15*0 1 15*0 1 15*0 1 15*0 1 15*0 1 15*0 1 15*0 1 15*0 1
  //   15*0 1 15*0 1 15*0 1 15*0 1 15*0 1 15*0 1 15*0 1 15*0 1 15*0 1 15*0 1 15*0 1 15*0 1 15*0 1 15*0 1
  //   15*0 1 15*0 1 15*0 1 15*0 1 15*0 1 15*0 1 15*0 1 15*0 1 15*0 1 15*0 1 15*0 1 15*0 1 15*0 1 15*0 1
  //   15*0 1 15*0 1 15*0 1 15*0 1 15*0 1 15*0 1 15*0 1 15*0 1 15*0 1 15*0 1 15*0 1 15*0 1 15*0 1 15*0 1
  //   15*0 1 15*0 1 15*0 1 15*0 1 15*0 1 15*0 1 15*0 1 15*0 1 15*0 1 15*0 1 15*0 1 15*0 1 15*0 1 15*0 1
  //   15*0 1 15*0 1 15*0 1 15*0 1 15*0 1 15*0 1 15*0 1 15*0 1 15*0 1 15*0 1 15*0 1 15*0 1 15*0 1 15*0 1
  //   15*0 1 15*0 1 15*0 1 15*0 1 15*0 1 15*0 1 15*0 1 15*0 1 15*0 1 15*0 1 15*0 1 15*0 1 15*0 1 15*0 1
  //   15*0 1 15*0 1 15*0 1 15*0 1 15*0 1 15*0 1 15*0 1 15*0 1 15*0 1 15*0 1 15*0 1 15*0 1 15*0 1 15*0 1
  //   18*0 1 20*0 1 15*0 1 11*0 1 20*0 1 10*0 1 20*0 1 12*0 80 41 14*0 80 41 10*0 1 15*0 1 19*0 80 41 10*0
  //   1 19*0 80 41 9*0 11 15*0 31 15*0 21 15*0 4 8 31 13*0 20 4 8 1 12*0 4 8 30 4 8 30 5*0 80 41 0 0 0 20
  //   4 8 60 4 8 80 0 1 7*0 1 14*0 1 15*0 1 15*0 1 15*0 1 15*0 1 15*0 1 15*0 1 15*0 1 15*0 1 15*0 1 15*0 1
  //   15*0 1 15*0 1 15*0 1 15*0 1 15*0 1 15*0 1 15*0 1 15*0 1 15*0 1 15*0 1 15*0 1 15*0 1 15*0 1 15*0 1
  //   15*0 1 15*0 1 15*0 1 15*0 1 15*0 1 15*0 1 15*0 1 15*0 1 15*0 1 15*0 1 15*0 1 15*0 1 15*0 1 15*0 1
  //   15*0 1 15*0 1 15*0 1 15*0 1 15*0 1 15*0 1 15*0 1 15*0 1 15*0 1 15*0 1 15*0 1 15*0 1 15*0 1 15*0 1
  //   15*0 1 15*0 1 15*0 1 15*0 1 15*0 1 15*0 1 15*0 1 15*0 1 15*0 1 15*0 1 15*0 1 15*0 1 15*0 1 15*0 1
  //   15*0 1 15*0 1 15*0 1 15*0 1 15*0 1 15*0 1 15*0 1 15*0 1 15*0 1 15*0 1 15*0 1 15*0 1 15*0 1 15*0 1
  //   15*0 1 15*0 1 15*0 1 15*0 1 15*0 1 15*0 1 15*0 1 15*0 1 15*0 1 15*0 1 15*0 1 15*0 1 15*0 1 15*0 1
  //   15*0 1 15*0 1 15*0 1 15*0 1 15*0 1 15*0 1 15*0 1 15*0 1 15*0 1 15*0 1 15*0 1 15*0 1 15*0 1 15*0 1
  //   15*0 1 15*0 1 15*0 1 15*0 1 15*0 1 15*0 1 15*0 1 15*0 1 15*0 1 15*0 1 15*0 1 15*0 1 15*0 1 15*0 1
  //   15*0 1 15*0 1 15*0 1 15*0 1 15*0 1 15*0 1 15*0 1 15*0 1 15*0 1 15*0 1 15*0 1 15*0 1 15*0 1 15*0 1
  //   15*0 1 15*0 1 15*0 1 15*0 1 15*0 1 15*0 1 15*0 1 15*0 1 15*0 1 15*0 1 15*0 1 15*0 1 15*0 1 15*0 1
  //   15*0 1 15*0 1 15*0 1 15*0 1 15*0 1 15*0 1 15*0 1 15*0 1 15*0 1 15*0 1 15*0 1 15*0 1 15*0 1 15*0 1
  //   15*0 1 15*0 1 15*0 1 15*0 1 15*0 1 15*0 1 15*0 1 15*0 1 15*0 1 15*0 1 15*0 1 15*0 1 15*0 1 15*0 1
  //   15*0 1 15*0 1 15*0 1 15*0 1 15*0 1 15*0 1 15*0 1 15*0 1 15*0 1 15*0 1 15*0 1 15*0 1 15*0 1 15*0 1
  //   15*0 1 15*0 1 15*0 1 15*0 1 15*0 1 15*0 1 15*0 1 15*0 1 15*0 1 15*0 1 15*0 1 15*0 1 15*0 1 15*0 1
  //   15*0 1 15*0 1 15*0 1 15*0 1 15*0 1 15*0 1 15*0 1 15*0 1 15*0 1 15*0 1 15*0 1 15*0 1 15*0 1 15*0 1
  //   15*0 1 15*0 1 15*0 1 15*0 1 15*0 1 15*0 1 15*0 1 15*0 1 15*0 1 15*0 1 15*0 1 15*0 1 15*0 1 18*0 1
  //   20*0 1 15*0 1 11*0 1 20*0 1 10*0 1 20*0 1 12*0 80 41 10*0 1 19*0 80 41 14*0 80 41 10*0 1 15*0 1 19*0
  //   80 41 9*0 11 15*0 31 15*0 21 15*0 4 8 31 13*0 20 4 8 1 12*0 4 8 30 4 8 30 5*0 80 41 0 0 0 20 4 8 60
  //   4 8 80 0 1 7*0 1 14*0 1 15*0 1 15*0 1 15*0 1 15*0 1 15*0 1 1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
endmodule

module stack_pointer (
  input  CLK,
  input  [1:0] MODE,
  input  HO,
  input  LO,
  output [7:0] out_bus
);

  wire and_1_out, counter_2_carry, decoder_1_out0, decoder_1_out1, decoder_1_out2, decoder_1_out3, or_1_out,
       or_2_out, or_3_out;
  wire [7:0] counter_1_q, counter_2_q;

  // NoConnect on decoder_1_out0
  Decoder #(.enable("false"), .select(2)) decoder_1 (
    .out0(decoder_1_out0), .out1(decoder_1_out1), .out2(decoder_1_out2), .out3(decoder_1_out3), .sel(MODE));
  or or_1 (or_1_out, decoder_1_out2, decoder_1_out3);
  and and_1 (and_1_out, or_1_out, counter_2_carry);
  or or_2 (or_2_out, decoder_1_out1, decoder_1_out2, decoder_1_out3);
  or or_3 (or_3_out, decoder_1_out1, and_1_out);
  Counter counter_1 (
    .load(decoder_1_out1), .up(decoder_1_out2), .count(or_3_out), .clk(CLK), .D({8{1'b1}}), .Q(counter_1_q));  // open: clr, carry
  Counter counter_2 (
    .load(decoder_1_out1), .up(decoder_1_out2), .count(or_2_out), .clk(CLK), .D({8{1'b1}}),
    .carry(counter_2_carry), .Q(counter_2_q));  // open: clr
  assign out_bus = HO ? counter_1_q : 8'bz;  // Controlled_Buffer controlled_buffer_1
  assign out_bus = LO ? counter_2_q : 8'bz;  // Controlled_Buffer controlled_buffer_2
endmodule
